// Logisim project logisim.circ as structural Verilog: 4 circuits, main circuit Problem 2
module Problem_2 (
);

  wire and_1_out, button_1_out, nand_1_out, nand_2_out, not_1_out, not_2_out, not_3_out, or_1_out, or_2_out;

  Button button_1 (.out(button_1_out));
  nand nand_1 (nand_1_out, ~not_1_out, button_1_out);  // NAND_Gate
  and and_1 (and_1_out, not_2_out, not_1_out);
  nand nand_2 (nand_2_out, button_1_out, not_1_out);
  or or_1 (or_1_out, nand_1_out, not_3_out);
  not not_1 (not_1_out, or_1_out);
  LED led_1 (.in(not_1_out));
  not not_2 (not_2_out, not_1_out);
  not not_3 (not_3_out, or_2_out);
  or or_2 (or_2_out, and_1_out, nand_2_out);
endmodule

module Problem_3 (
  input  Reset,
  input  I_O_Enable,
  input  _1_Bit,
  input  _2_Bit,
  input  _4_Bit,
  input  _8_Bit,
  output A_C,
  output D0,
  output D1,
  output D2,
  output D3,
  output Engine_Starter,
  output Wipers
);

  Pr3_IO_Controller pr3_io_controller_1 (
    .Reset(Reset), .IO_Enable(I_O_Enable), ._1_bit(_1_Bit), ._2_bit(_2_Bit), ._4_bit(_4_Bit),
    ._8_bit(_8_Bit), .A_C(A_C), .D0(D0), .D1(D1), .D2(D2), .D3(D3), .Engine_Starter(Engine_Starter),
    .Wipers(Wipers));

  // Notes on the sheet:
  //   Micro Controller
endmodule

module Pr3_IO_Controller (
  input  Reset,
  input  IO_Enable,
  input  _1_bit,
  input  _2_bit,
  input  _4_bit,
  input  _8_bit,
  output A_C,
  output D0,
  output D1,
  output D2,
  output D3,
  output Engine_Starter,
  output Wipers
);

  wire and_1_out, and_2_out, and_3_out, and_4_out, and_5_out, and_6_out, and_7_out, and_8_out, and_9_out,
       and_10_out, and_11_out, and_12_out, and_13_out, and_14_out, and_15_out, not_1_out, not_2_out,
       not_3_out, not_4_out, not_5_out, not_6_out;

  not not_1 (not_1_out, Reset);
  and and_1 (and_1_out, IO_Enable, not_2_out);
  not not_2 (not_2_out, IO_Enable);
  not not_3 (not_3_out, _1_bit);
  not not_4 (not_4_out, _2_bit);
  not not_5 (not_5_out, _4_bit);
  not not_6 (not_6_out, _8_bit);
  D_Flip_Flop d_ff_1 (.clk(and_2_out), .D(not_1_out), .Q(A_C));  // open: Qn, preset, en, reset
  and and_2 (and_2_out, and_1_out, and_3_out);
  and and_3 (and_3_out, not_3_out, not_4_out, not_5_out, not_6_out);
  D_Flip_Flop d_ff_2 (.clk(and_4_out), .D(not_1_out), .Q(D0));  // open: Qn, preset, en, reset
  and and_4 (and_4_out, and_1_out, and_5_out);
  and and_5 (and_5_out, _1_bit, not_4_out, not_5_out, not_6_out);
  D_Flip_Flop d_ff_3 (.clk(and_6_out), .D(not_1_out), .Q(D1));  // open: Qn, preset, en, reset
  and and_6 (and_6_out, and_1_out, and_7_out);
  and and_7 (and_7_out, not_3_out, _2_bit, not_5_out, not_6_out);
  D_Flip_Flop d_ff_4 (.clk(and_8_out), .D(not_1_out), .Q(D2));  // open: Qn, preset, en, reset
  and and_8 (and_8_out, and_1_out, and_9_out);
  and and_9 (and_9_out, _1_bit, _2_bit, not_5_out, not_6_out);
  D_Flip_Flop d_ff_5 (.clk(and_10_out), .D(not_1_out), .Q(D3));  // open: Qn, preset, en, reset
  and and_10 (and_10_out, and_1_out, and_11_out);
  and and_11 (and_11_out, not_3_out, not_4_out, _4_bit, not_6_out);
  D_Flip_Flop d_ff_6 (.clk(and_12_out), .D(not_1_out), .Q(Engine_Starter));  // open: Qn, preset, en, reset
  and and_12 (and_12_out, and_1_out, and_13_out);
  and and_13 (and_13_out, _1_bit, not_4_out, _4_bit, not_6_out);
  D_Flip_Flop d_ff_7 (.clk(and_14_out), .D(not_1_out), .Q(Wipers));  // open: Qn, preset, en, reset
  and and_14 (and_14_out, and_1_out, and_15_out);
  and and_15 (and_15_out, not_3_out, _2_bit, _4_bit, not_6_out);
endmodule

module Manually_Implemented_D_Flip_Flop (
  input  Data,
  input  Clock,
  output Q,
  output Q_prime
);

  wire and_1_out, and_2_out, not_1_out, or_1_out, or_2_out;

  not not_1 (not_1_out, Data);
  and and_1 (and_1_out, not_1_out, Clock);
  and and_2 (and_2_out, Data, Clock);
  or or_1 (or_1_out, and_1_out, Q_prime);
  or or_2 (or_2_out, Q, and_2_out);
  not not_2 (Q, or_1_out);
  not not_3 (Q_prime, or_2_out);
endmodule
