// Logisim project cpu.circ as structural Verilog: 3 circuits, main circuit CPU
module Memory (
  input  [7:0] Address,
  input  [7:0] Data_In,
  input  [1:0] Operation,
  output [7:0] Data_Out
);

  wire not_1_out, or_1_out, RAM_R_out, RAM_W_out, ROM_R_out;

  assign Data_Out = RAM_W_out ? Data_In : 8'bz;  // Controlled_Buffer controlled_buffer_1
  and ROM_R (ROM_R_out, Operation[0], ~Operation[1]);  // AND_Gate
  ROM rom_1 (.addr(Address), .data(Data_Out), .sel(ROM_R_out));
  and RAM_R (RAM_R_out, ~Operation[0], Operation[1]);  // AND_Gate
  or or_1 (or_1_out, RAM_R_out, RAM_W_out);
  not not_1 (not_1_out, RAM_W_out);
  and RAM_W (RAM_W_out, Operation[0], Operation[1]);
  RAM #(.bus("asynch")) ram_1 (.addr(Address), .data(Data_Out), .sel(or_1_out), .ld(not_1_out));  // open: clr

  // Notes on the sheet:
  //   contents of rom_1 (hex, n*v repeats v):
  //   2 11 3 4 0 5 6 7 8 9 a b c d e f
endmodule

module CPU (
);

  wire and_1_out, and_2_out, and_3_out, and_4_out, and_6_out, and_7_out, and_8_out, and_9_out, clock_1_out,
       clock_2_out, Decode, decoder_1_out0, decoder_1_out1, decoder_1_out2, decoder_1_out3, decoder_1_out4,
       decoder_1_out5, decoder_1_out6, decoder_1_out7, decoder_1_out8, decoder_1_out9, decoder_2_out0,
       decoder_2_out1, decoder_2_out2, decoder_2_out3, decoder_2_out4, decoder_2_out5, decoder_2_out6,
       decoder_2_out7, decoder_2_out8, decoder_2_out9, decoder_2_out10, decoder_2_out11, decoder_2_out12,
       decoder_2_out13, decoder_2_out14, decoder_2_out15, MemSet_do_Write, or_1_out, undriven;
  wire [1:0] controlled_buffer_1_out, M_Select;
  wire [3:0] controlled_buffer_3_out, controlled_buffer_20_out, rA_R, rA_W, rB_R, rB_W, register_6_q;
  wire [7:0] adder_1_out, adder_2_out, adder_3_out, adder_4_out, adder_5_out, controlled_buffer_2_out,
       controlled_buffer_26_out, controlled_buffer_27_out, M_Addr, M_In, M_Out, MemSet_addr, npc_R, npc_W,
       PC_In, PC_Out, register_7_q, register_8_q, register_9_q, register_11_q, register_12_q,
       register_file_1_read_data, val_R, val_W;

  assign controlled_buffer_1_out = MemSet_do_Write ? 2'b11 : 2'bz;  // Controlled_Buffer controlled_buffer_1
  assign controlled_buffer_2_out = MemSet_do_Write ? MemSet_addr : 8'bz;  // Controlled_Buffer controlled_buffer_2
  Memory memory_1 (.Address(M_Addr), .Data_Out(M_Out), .Data_In(M_In), .Operation(M_Select));
  Register register_1 (.D(PC_In), .Q(PC_Out), .clk(undriven));  // open: en, clr
  Register #(.width(4)) register_2 (.D(rA_W), .Q(rA_R), .clk(Decode));  // open: en, clr
  Register #(.width(4)) register_3 (.D(rB_W), .Q(rB_R), .clk(Decode));  // open: en, clr
  Register register_4 (.D(val_W), .Q(val_R), .clk(Decode));  // open: en, clr
  Register register_5 (.D(npc_W), .Q(npc_R), .clk(Decode));  // open: en, clr
  Adder adder_1 (.a(PC_Out), .b(8'h3), .out(adder_1_out));  // open: cin, cout
  Adder adder_2 (.a(PC_Out), .b(8'h1), .out(adder_2_out));  // open: cin, cout
  Adder adder_3 (.a(PC_Out), .b(8'h2), .out(adder_3_out));  // open: cin, cout
  Multiplexer #(.select(4), .width(2)) multiplexer_1 (
    .in0(2'b00), .in1(2'b01), .in2(2'b01), .in3(2'b01), .in8(controlled_buffer_1_out), .out(M_Select),
    .sel(register_6_q));  // open: in4, in5, in6, in7, in9, in10, in11, in12, in13, in14, in15, en
  Multiplexer #(.select(4), .width(8)) multiplexer_2 (
    .in0(adder_1_out), .in1(PC_Out), .in2(adder_2_out), .in3(adder_3_out), .in8(controlled_buffer_2_out),
    .out(M_Addr), .sel(register_6_q));  // open: in4, in5, in6, in7, in9, in10, in11, in12, in13, in14, in15, en
  assign controlled_buffer_3_out = decoder_2_out0 ? 4'b0001 : 4'bz;  // Controlled_Buffer controlled_buffer_3
  assign controlled_buffer_3_out = decoder_2_out1 ? 4'b0010 : 4'bz;  // Controlled_Buffer controlled_buffer_4
  assign controlled_buffer_3_out = decoder_2_out2 ? 4'b0011 : 4'bz;  // Controlled_Buffer controlled_buffer_5
  assign controlled_buffer_3_out = decoder_2_out3 ? 4'b0100 : 4'bz;  // Controlled_Buffer controlled_buffer_6
  assign controlled_buffer_3_out = decoder_2_out4 ? 4'b0101 : 4'bz;  // Controlled_Buffer controlled_buffer_7
  assign controlled_buffer_3_out = decoder_2_out5 ? 4'b0110 : 4'bz;  // Controlled_Buffer controlled_buffer_8
  assign controlled_buffer_3_out = decoder_2_out6 ? 4'b0111 : 4'bz;  // Controlled_Buffer controlled_buffer_9
  assign controlled_buffer_3_out = decoder_2_out7 ? 4'b1000 : 4'bz;  // Controlled_Buffer controlled_buffer_10
  assign controlled_buffer_3_out = decoder_2_out8 ? 4'b1001 : 4'bz;  // Controlled_Buffer controlled_buffer_11
  assign controlled_buffer_3_out = decoder_2_out9 ? 4'b1010 : 4'bz;  // Controlled_Buffer controlled_buffer_12
  assign controlled_buffer_3_out = decoder_2_out10 ? 4'b1011 : 4'bz;  // Controlled_Buffer controlled_buffer_13
  assign controlled_buffer_3_out = decoder_2_out11 ? 4'b1100 : 4'bz;  // Controlled_Buffer controlled_buffer_14
  assign controlled_buffer_3_out = decoder_2_out12 ? 4'b1101 : 4'bz;  // Controlled_Buffer controlled_buffer_15
  assign controlled_buffer_3_out = decoder_2_out13 ? 4'b1110 : 4'bz;  // Controlled_Buffer controlled_buffer_16
  assign controlled_buffer_3_out = decoder_2_out14 ? 4'b1111 : 4'bz;  // Controlled_Buffer controlled_buffer_17
  assign controlled_buffer_3_out = decoder_2_out15 ? 4'b0000 : 4'bz;  // Controlled_Buffer controlled_buffer_18
  Register #(.width(4)) register_6 (.D(controlled_buffer_3_out), .Q(register_6_q), .clk(clock_1_out));  // open: en, clr
  Clock clock_1 (.out(clock_1_out));
  Decoder #(.select(4)) decoder_1 (
    .out0(decoder_1_out0), .out1(decoder_1_out1), .out2(decoder_1_out2), .out3(decoder_1_out3),
    .out4(decoder_1_out4), .out5(decoder_1_out5), .out6(decoder_1_out6), .out7(decoder_1_out7),
    .out8(decoder_1_out8), .out9(decoder_1_out9), .sel(register_6_q));  // open: out10, out11, out12, out13, out14, out15, en
  Clock clock_2 (.out(clock_2_out));
  Decoder #(.select(4)) decoder_2 (
    .out0(decoder_2_out0), .out1(decoder_2_out1), .out2(decoder_2_out2), .out3(decoder_2_out3),
    .out4(decoder_2_out4), .out5(decoder_2_out5), .out6(decoder_2_out6), .out7(decoder_2_out7),
    .out8(decoder_2_out8), .out9(decoder_2_out9), .out10(decoder_2_out10), .out11(decoder_2_out11),
    .out12(decoder_2_out12), .out13(decoder_2_out13), .out14(decoder_2_out14), .out15(decoder_2_out15),
    .sel(register_6_q));  // open: en
  and and_1 (and_1_out, clock_2_out, decoder_1_out1);
  and and_2 (and_2_out, clock_2_out, decoder_1_out2);
  and and_3 (and_3_out, clock_2_out, decoder_1_out3);
  and and_4 (and_4_out, clock_2_out, decoder_1_out4);
  and and_5 (Decode, clock_2_out, decoder_1_out5);
  and and_6 (and_6_out, clock_2_out, decoder_1_out6);
  and and_7 (and_7_out, clock_2_out, decoder_1_out7);
  and and_8 (and_8_out, clock_2_out, decoder_1_out8);
  and and_9 (and_9_out, clock_2_out, decoder_1_out9);
  Adder adder_4 (.a(npc_R), .b(PC_Out), .out(adder_4_out));  // open: cin, cout
  Register #(.trigger("high")) register_7 (.D(M_Out), .Q(register_7_q), .clk(and_1_out));  // open: en, clr
  Register #(.trigger("high")) register_8 (.D(M_Out), .Q(register_8_q), .clk(and_2_out));  // open: en, clr
  Register #(.trigger("high")) register_9 (.D(M_Out), .Q(register_9_q), .clk(and_3_out));  // open: en, clr
  Register #(.trigger("high")) register_10 (.D(M_Out), .clk(and_4_out));  // open: en, Q, clr
  assign PC_In = and_9_out ? adder_4_out : 8'bz;  // Controlled_Buffer controlled_buffer_19
  assign controlled_buffer_20_out = and_6_out ? rA_R : 4'bz;  // Controlled_Buffer controlled_buffer_20
  or or_1 (or_1_out, and_6_out, and_7_out);
  assign controlled_buffer_20_out = and_7_out ? rB_R : 4'bz;  // Controlled_Buffer controlled_buffer_21
  and MEMSET (MemSet_do_Write, ~register_7_q[0], register_7_q[1], ~register_7_q[2], ~register_7_q[3], ~register_7_q[4], ~register_7_q[5], ~register_7_q[6], ~register_7_q[7]);  // AND_Gate
  assign {rB_W, rA_W} = MemSet_do_Write ? register_8_q : 8'bz;  // Controlled_Buffer controlled_buffer_22
  assign val_W = MemSet_do_Write ? register_9_q : 8'bz;  // Controlled_Buffer controlled_buffer_23
  assign npc_W = MemSet_do_Write ? 8'h2 : 8'bz;  // Controlled_Buffer controlled_buffer_24
  Register_File register_file_1 (
    .Addr(controlled_buffer_20_out), .Write(1'b0), .Read(or_1_out), .Read_Data(register_file_1_read_data));  // open: Write_Data
  Adder adder_5 (.a(register_11_q), .b(val_R), .out(adder_5_out));  // open: cin, cout
  assign MemSet_addr = and_8_out ? adder_5_out : 8'bz;  // Controlled_Buffer controlled_buffer_25
  // AND_Gate MEMLD has open pins: in0=register_7_q[0], in1=register_7_q[1], in2=register_7_q[2], in3=register_7_q[3], in4=register_7_q[4], in5=register_7_q[5], in6=register_7_q[6], in7=register_7_q[7], out=open
  assign controlled_buffer_26_out = and_6_out ? register_file_1_read_data : 8'bz;  // Controlled_Buffer controlled_buffer_26
  assign controlled_buffer_27_out = and_7_out ? register_file_1_read_data : 8'bz;  // Controlled_Buffer controlled_buffer_27
  assign M_In = and_8_out ? register_12_q : 8'bz;  // Controlled_Buffer controlled_buffer_28
  // AND_Gate REGSET has open pins: in0=register_7_q[0], in1=register_7_q[1], in2=register_7_q[2], in3=register_7_q[3], in4=register_7_q[4], in5=register_7_q[5], in6=register_7_q[6], in7=register_7_q[7], out=open
  Register #(.trigger("high")) register_11 (
    .D(controlled_buffer_26_out), .Q(register_11_q), .clk(and_6_out));  // open: en, clr
  Register #(.trigger("high")) register_12 (
    .D(controlled_buffer_27_out), .Q(register_12_q), .clk(and_7_out));  // open: en, clr
  // AND_Gate ADD has open pins: in0=register_7_q[0], in1=register_7_q[1], in2=register_7_q[2], in3=register_7_q[3], in4=register_7_q[4], in5=register_7_q[5], in6=register_7_q[6], in7=register_7_q[7], out=open
endmodule

module Register_File (
  input  [7:0] Write_Data,
  input  [3:0] Addr,
  input  Write,
  input  Read,
  output [7:0] Read_Data
);

  wire decoder_1_out1, decoder_1_out2, decoder_1_out3, decoder_1_out4, decoder_1_out6, decoder_1_out7,
       decoder_1_out8, decoder_1_out9, xor_1_out;
  wire [3:0] adder_1_out, controlled_buffer_1_out, controlled_buffer_3_out;
  wire [7:0] register_1_q, register_2_q, register_3_q, register_4_q;

  xor xor_1 (xor_1_out, Write, Read);
  assign controlled_buffer_1_out = Write ? 4'b0101 : 4'bz;  // Controlled_Buffer controlled_buffer_1
  assign controlled_buffer_1_out = Read ? 4'b0000 : 4'bz;  // Controlled_Buffer controlled_buffer_2
  Adder #(.width(4)) adder_1 (.a(Addr), .b(controlled_buffer_1_out), .out(adder_1_out));  // open: cin, cout
  assign controlled_buffer_3_out = xor_1_out ? adder_1_out : 4'bz;  // Controlled_Buffer controlled_buffer_3
  Decoder #(.select(4)) decoder_1 (
    .out1(decoder_1_out1), .out2(decoder_1_out2), .out3(decoder_1_out3), .out4(decoder_1_out4),
    .out6(decoder_1_out6), .out7(decoder_1_out7), .out8(decoder_1_out8), .out9(decoder_1_out9),
    .sel(controlled_buffer_3_out));  // open: out0, out5, out10, out11, out12, out13, out14, out15, en
  assign Read_Data = decoder_1_out1 ? register_1_q : 8'bz;  // Controlled_Buffer controlled_buffer_4
  Register register_1 (.D(Write_Data), .Q(register_1_q), .clk(decoder_1_out6));  // open: en, clr
  Register register_2 (.D(Write_Data), .Q(register_2_q), .clk(decoder_1_out7));  // open: en, clr
  assign Read_Data = decoder_1_out2 ? register_2_q : 8'bz;  // Controlled_Buffer controlled_buffer_5
  Register register_3 (.D(Write_Data), .Q(register_3_q), .clk(decoder_1_out8));  // open: en, clr
  Register register_4 (.D(Write_Data), .Q(register_4_q), .clk(decoder_1_out9));  // open: en, clr
  assign Read_Data = decoder_1_out3 ? register_3_q : 8'bz;  // Controlled_Buffer controlled_buffer_6
  assign Read_Data = decoder_1_out4 ? register_4_q : 8'bz;  // Controlled_Buffer controlled_buffer_7
endmodule
